# Fritzing sketch schemat (saved by Fritzing 1.0.6)

parts:
  U2 = ESP32S-HiLetgo [part_number=ESP32S-HiLetgo]
  DRV8825_Stepper_controller = DRV 8825 Stepper Motor Carrier, High Current [part_number="DRV 8825"]
  RGB_Diode = RGB LED - (4 legs) [color="Red (633nm)" current=0.030A package="5 mm [THT]"]
  S2 = Pushbutton [package="[THT]"]
  U1 = POT [knob_status=50% power=0.5W package=pot_mammoth]
  M1 = RioRand LM2596  # not connected
  Display1 = LCD screen 16x2 I2C [part_number=101290]
  Mod1 = KY-024 Linear Hall Magnetic Sensor Module [package="Breakout board"]
  Part1 = Adafruit SPI Flash SD Card [part_number="Adafruit #4899"]
  J1 = Basic Servo  # not connected
  C1 = Capacitor Polarized [package=cpol-radial-10uf-25v]
  NEMA17_Stepper_Motor = Stepper Motor - Bipolar

nets:
  N1: U2.GPIO34, U1.A
  N2: U2.GPIO35, Mod1.A0
  N3: U2.GPIO33, DRV8825_Stepper_controller.STEP
  N4: U2.GPIO26, DRV8825_Stepper_controller.DIRECTION
  N5: U2.GPIO27, RGB_Diode.green_cathode
  N6: U2.GPIO14, RGB_Diode.common_anode
  N7: U2.GND, DRV8825_Stepper_controller.GROUND_LOG, RGB_Diode.blue_cathode
  N8: U2.GPIO13, RGB_Diode.red_cathode
  N9: U2.VIN, Mod1.+
  N10: U2.GPIO16, S2.Pin_1, S2.Pin_2
  N11: U2.GPIO5, Part1.SS
  N12: U2.GPIO18, Part1.SCK
  N13: U2.GPIO19, Part1.MISO_3.3V
  N14: U2.GPIO21, Display1.SDA
  N15: U2.GPIO22, Display1.SCL
  N16: U2.GPIO23, Part1.MOSI
  N17: DRV8825_Stepper_controller.VOLTAGE_ST/_MT, C1.-
  N18: DRV8825_Stepper_controller.GROUND_ST/_MT, C1.+
  N19: DRV8825_Stepper_controller.OUT_2B, NEMA17_Stepper_Motor.A
  N20: DRV8825_Stepper_controller.OUT_2A, NEMA17_Stepper_Motor.C
  N21: DRV8825_Stepper_controller.OUT_1A, NEMA17_Stepper_Motor.B
  N22: DRV8825_Stepper_controller.OUT_1B, NEMA17_Stepper_Motor.D

custom parts:
  ESP32S-HiLetgo: HiLetgo ESP-WROOM-32 ESP32 ESP-32S Development Board 2.4GHz Dual-Mode WiFi + Bluetooth Dual Cores Microcontroller The ESP32 integrated with Antenna switches, RF Balun, power amplifiers, low-noise amplifiers, filters, and management modules, and the entire solution occupies the least area of PCB. 2.4 GHz Wi-Fi plus Bluetooth dual-mode chip, with TSMC Ultra-low power consumption 40nm technology,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
  KY-024 Linear Hall Magnetic Sensor Module: KY-024 Linear Hall Magnetic Sensor Module reacts iin the presence of a magnetic field.
  Adafruit SPI Flash SD Card: This breakout is for a fascinating chip - it looks like an SPI Flash storage chip (like the GD25Q16) but its really an SD card, in an SMT chip format. What that means is that you wire up like an SD card breakout, and use the SD card libraries you already have for your microcontroller. For example, you can use the built in SD library in Arduino, or for CircuitPython we have an sdcard library.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
